# Fritzing sketch prism-dev-board-1.0 (saved by Fritzing 0.9.3b)
breadboards: 1

parts:
  U1 = NodeMCU V1.0
  Squix1 = OLED 0.96" 128x64 I2C SSD1306
  S1 = Pushbutton [package="[THT]"]
  R1 = Resistor [tolerance=±5% resistance=10k package="0805 [SMD]"]

nets:
  N1: U1.D1, Squix1.SCL
  N2: U1.D2, Squix1.SCA
  3V3: U1.3V3, Squix1.VCC, S1.Pin_3, S1.Pin_4
  GND: U1.GND, Squix1.GND, R1.Pin_0
  N3: U1.D6, S1.Pin_1, S1.Pin_2, R1.Pin_1

custom parts:
  NodeMCU V1.0: ESP8266 based NodeMCU
